# Fritzing sketch DoorBellSwitch (saved by Fritzing 0.9.3b)
circuit board: 3.5cm x 3.5cm
breadboards: 1

parts:
  ESP-01 = ESP8266 WiFi Module [part_number=ESP8266]
  HLK-PM3 = HLK-PM01
  J1 = Screw terminal - 2 pins [package=THT]
  R1_1KΩ = Resistor [tolerance=±5% resistance=220 package=THT]
  J2 = screw terminal, 3 pins

nets:
  N1: ESP-01.VCC, HLK-PM3.+Vo, R1_1KΩ.Pin_0
  N2: ESP-01.GPIO_0, J2.pin1
  N3: ESP-01.GPIO_2, J2.pin3
  N4: ESP-01.CH_PD, R1_1KΩ.Pin_1
  N5: ESP-01.GND, HLK-PM3.-Vo, J2.pin2
  N6: HLK-PM3.AC#0, J1.pin2
  N7: HLK-PM3.AC#1, J1.pin1

notes:
  DoorBellSwitch

custom parts:
  ESP8266 WiFi Module: Generic WiFi Module based on the ESP8266 with onboard PCB antenna and UART communications
